# Fritzing sketch Board_10 (saved by Fritzing 0.9.2b)
circuit board: 7.1292cm x 7.42442cm
circuit board: 6cm x 2.2cm
circuit board: 6.5cm x 3cm
circuit board: 8.82977cm x 11.5238cm
breadboards: 1

parts:
  LED1 = RGB LED (com. cathode, rbg) [package="5 mm [THT]"]
  LED2 = RGB LED (com. cathode, rbg) [package="5 mm [THT]"]
  LED3 = RGB LED (com. cathode, rbg) [package="5 mm [THT]"]  # not connected
  LED4 = RGB LED (com. cathode, rbg) [package="5 mm [THT]"]  # not connected
  LED5 = RGB LED (com. cathode, rbg) [package="5 mm [THT]"]  # not connected
  LED7 = RGB LED (com. cathode, rbg) [package="5 mm [THT]"]  # not connected
  LED8 = RGB LED (com. cathode, rbg) [package="5 mm [THT]"]  # not connected
  LED9 = RGB LED (com. cathode, rbg) [package="5 mm [THT]"]  # not connected
  LED11 = RGB LED (com. cathode, rbg) [package="5 mm [THT]"]  # not connected
  LED12 = RGB LED (com. cathode, rbg) [package="5 mm [THT]"]  # not connected
  LED13 = RGB LED (com. cathode, rbg) [package="5 mm [THT]"]  # not connected
  LED15 = RGB LED (com. cathode, rbg) [package="5 mm [THT]"]  # not connected
  LED16 = RGB LED (com. cathode, rbg) [package="5 mm [THT]"]  # not connected
  5_V = Battery block 9V
  LED10 = RGB LED (com. cathode, rbg) [package="5 mm [THT]"]  # not connected
  LED14 = RGB LED (com. cathode, rbg) [package="5 mm [THT]"]  # not connected
  LED6 = RGB LED (com. cathode, rbg) [package="5 mm [THT]"]  # not connected
  LED19 = RGB LED (com. cathode, rbg) [package="5 mm [THT]"]  # not connected
  LED20 = RGB LED (com. cathode, rbg) [package="5 mm [THT]"]  # not connected
  LED21 = RGB LED (com. cathode, rbg) [package="5 mm [THT]"]  # not connected
  LED22 = RGB LED (com. cathode, rbg) [package="5 mm [THT]"]  # not connected
  1000µF = Electrolytic Capacitor [capacitance=1000µF package="300 mil [THT, electrolytic]"]
  TIP120 = pnp-Powertransistor [package="TO220 [THT]"]
  2_2kΩ = Resistor [tolerance=±5% resistance=2.2k package=THT]
  Q2 = pnp-Powertransistor [package="TO220 [THT]"]
  R2 = Resistor [tolerance=±5% resistance=2.2k package=THT]
  R3 = Resistor [tolerance=±5% resistance=2.2k package=THT]
  Q3 = pnp-Powertransistor [package="TO220 [THT]"]
  J2 = female pin header, 2 pins [form="♀ (female)"]
  J3 = female pin header, 2 pins [form="♀ (female)"]  # not connected
  J4 = female pin header, 2 pins [form="♀ (female)"]  # not connected
  S3 = SWITCH-MOMENTARY-2 [package=tactile_switch_smd-2]  # not connected
  10kΩ = Resistor [tolerance=±5% resistance=10k package=THT]
  Diode = Zener Diode [part_number=1N4732A breakdown_voltage=3.6V package="300 mil [THT]"]
  220Ω = Resistor [tolerance=±5% resistance=220 package=THT]
  LED = LEDs [package=led10mm]  # not connected
  R7 = Resistor [tolerance=±5% resistance=220 package=THT]
  LED24 = LEDs [package=led10mm]  # not connected
  LED25 = LEDs [package=led10mm]  # not connected
  R8 = Resistor [tolerance=±5% resistance=220 package=THT]
  LED26 = RGB LED (com. cathode, rbg) [package="5 mm [THT]"]  # not connected
  LED28 = RGB LED (com. cathode, rbg) [package="5 mm [THT]"]  # not connected
  LED29 = RGB LED (com. cathode, rbg) [package="5 mm [THT]"]  # not connected
  470Ω = Resistor [tolerance=±5% resistance=470 package=THT]
  12_V1 = Battery block 9V
  12_V2 = Battery block 9V
  5_V1 = Battery block 9V
  5_V2 = Battery block 9V
  Bauteil1 = Arduino Yun

nets:
  N1: LED1.red_anode, LED2.green_anode
  N2: LED1.common_cathode, LED2.common_cathode
  N3: LED1.blue_anode, LED2.blue_anode
  N4: LED1.green_anode, 470Ω.Pin_0
  N5: 5_V.-, 1000µF.-, TIP120.emitter, Q2.emitter, Q3.emitter, 10kΩ.Pin_0, 12_V2.-
  N6: 5_V.+, 1000µF.+, 12_V1.-, Bauteil1.VIN
  N7: TIP120.collector, J2.pin2, Diode.anode
  N8: 2_2kΩ.Pin_1, 220Ω.Pin_1, Bauteil1.D4
  N9: R2.Pin_1, R7.Pin_1, Bauteil1.D7
  N10: R3.Pin_1, R8.Pin_1, Bauteil1.ICSP_MISO, Bauteil1.D12/MISO
  N11: J2.pin1, Diode.cathode
  N12: 10kΩ.Pin_1, 12_V1.+, Bauteil1.D2
  N13: 470Ω.Pin_1, Bauteil1.D13/SCK
  N14: 12_V2.+, Bauteil1.D10_PWM/SS
  N15: 5_V1.-, 5_V2.-
  N16: 5_V1.+, 5_V2.+

notes:
  Dout
  TV
  12V
  5V
  LED
  Bell
  Rot.
  Secr.
  NBF LED
  +
  -
  in
  Din

custom parts:
  Arduino Yun: The new Arduino Yun is a microcontroller board based on the ATmega32u4 (datasheet) and the Atheros AR9331. The Atheros processor supports a Linux distribution based on OpenWRT named Linino. The board has built-in Ethernet and WiFi support, a USB-A port, micro-SD card slot, 20 digital input/output pins (of which 7 can be used as PWM outputs and 12 as analog inputs), a 16 MHz crystal oscillator,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
